# Fritzing sketch bracelet (saved by Fritzing 0.9.3b)
circuit board: 8.46667cm x 5.64444cm
breadboards: 1

parts:
  Composant1 = Arduino Nano (Rev3.0)
  LED1 = RGB LED (com. cathode, rgb) [package="5 mm [THT]"]
  LED2 = RGB LED (com. cathode, rgb) [package="5 mm [THT]"]
  R1 = Resistor [tolerance=±5% resistance=220 package=THT]
  R2 = Resistor [tolerance=±5% resistance=220 package=THT]
  R3 = Resistor [tolerance=±5% resistance=220 package=THT]
  R4 = Resistor [tolerance=±5% resistance=220 package=THT]
  R5 = Resistor [tolerance=±5% resistance=220 package=THT]
  R6 = Resistor [tolerance=±5% resistance=220 package=THT]
  S1 = Pushbutton [package=THT]

nets:
  N1: Composant1.GND, S1.leg1
  N2: Composant1.D2, R3.Pin_0
  N3: Composant1.D3, R2.Pin_0
  N4: Composant1.D4, R1.Pin_0
  N5: Composant1.D6, R6.Pin_0
  N6: Composant1.D7, R5.Pin_0
  N7: Composant1.D8, R4.Pin_0
  N8: LED1.common_cathode, LED2.common_cathode, S1.leg0
