# Fritzing sketch braceletSketch (saved by Fritzing 0.9.3b)
circuit board: 8.46667cm x 5.64444cm

parts:
  bluno = Arduino Nano (Rev3.0)
  LED_functionnement = RGB LED (com. cathode, rgb) [package="5 mm [THT]"]
  LED_operation = RGB LED (com. cathode, rgb) [package="5 mm [THT]"]
  R1 = Resistor [tolerance=±5% resistance=220 package=THT]
  R2 = Resistor [tolerance=±5% resistance=220 package=THT]
  R3 = Resistor [tolerance=±5% resistance=220 package=THT]
  R4 = Resistor [tolerance=±5% resistance=220 package=THT]
  R5 = Resistor [tolerance=±5% resistance=220 package=THT]
  R6 = Resistor [tolerance=±5% resistance=220 package=THT]
  S1 = Pushbutton [package=THT]

nets:
  N1: bluno.GND, S1.leg0
  N2: bluno.D2, R1.Pin_0
  N3: bluno.D3, R2.Pin_0
  N4: bluno.D4, R3.Pin_0
  N5: bluno.D6, R4.Pin_0
  N6: bluno.D8, R6.Pin_0
  N7: bluno.D10, R5.Pin_0
  N8: LED_functionnement.red_anode, R1.Pin_1
  N9: LED_functionnement.common_cathode, LED_operation.common_cathode, S1.leg1
  N10: LED_functionnement.green_anode, R2.Pin_1
  N11: LED_functionnement.blue_anode, R3.Pin_1
  N12: LED_operation.red_anode, R4.Pin_1
  N13: LED_operation.green_anode, R6.Pin_1
  N14: LED_operation.blue_anode, R5.Pin_1

// code stored in the sketch: bracelet.ino
int redPin= 7;
int greenPin = 6;
int bluePin = 5;
void setup() {
  pinMode(redPin, OUTPUT);
  pinMode(greenPin, OUTPUT);
  pinMode(bluePin, OUTPUT);
}
void loop() {
  
}
void setColor(int redValue, int greenValue, int blueValue) {
  analogWrite(redPin, redValue);
  analogWrite(greenPin, greenValue);
  analogWrite(bluePin, blueValue);
}
